# Fritzing sketch bpfilt (saved by Fritzing 0.9.3b)
circuit board: 8.46667cm x 5.64444cm
breadboards: 1

parts:
  U1 = OP37 - Low Noise, Precision, High Speed Op Amp [part_number=411]
  C1 = Ceramic Capacitor [capacitance=100nF package="200 mil [THT, multilayer]"]
  R1 = Resistor [tolerance=±5% resistance=1.71M package=THT]
  R2 = Resistor [tolerance=±5% resistance=855k package=THT]
  R3 = Resistor [tolerance=±5% resistance=22.5k package=THT]
  C2 = Ceramic Capacitor [capacitance=100nF package="100 mil [THT, multilayer]"]

nets:
  N1: U1.-IN, C1.1, R1.Pin_0
  GND: U1.+IN, R3.Pin_1
  Vout: U1.OUT, R1.Pin_1, C2.1
  N2: C1.0, R2.Pin_1, R3.Pin_0, C2.0
  Vin: R2.Pin_0
